# Fritzing sketch RightGloveDesign (saved by Fritzing 0.9.3b)
circuit board: 5.06961cm x 5.13924cm
breadboards: 1

parts:
  U1 = ATTINY13 [package=dip]
  BT2 = Bluetooth HC-05 Macho
  BT1 = Bluetooth HC-05 Macho
  LED1 = LED - 5mm [color="Red (633nm)" package="5 mm [THT]"]
  C1 = Tantalum Capacitor [capacitance="1 μF" package="C 6032 [SMD, tantalum]"]
  C2 = Electrolytic Capacitor [capacitance=1000μF package="1010 [SMD, electrolytic]"]
  IC1 = Voltage Regulator [package=to-220-alt]
  Vcc = Battery block 9V

nets:
  N1: U1.PB3(ADC3), LED1.anode
  N2: U1.PB4(ADC2), BT1.RXD
  GND: U1.GND, BT1.GND, LED1.cathode, C1.-
  N3: U1.PB1(MISO), BT2.TXD
  VCC: U1.VCC, BT2.VCC, BT1.VCC, C1.+, Vcc.+
  N4: BT2.GND, C2.+, Vcc.-
  N5: C2.-, IC1.IN
